// Logisim project Tic_Tac_Toe .circ as structural Verilog: 3 circuits, main circuit main
module _1_case_winner_detect (
  input  [1:0] in_1,
  input  [1:0] in_2,
  input  [1:0] in_3,
  output winner,
  output [1:0] Who
);

  wire or_1_out;
  wire [1:0] and_1_out, xnor_1_out, xnor_2_out;

  assign xnor_1_out = ~(in_1 ^ in_2);  // XNOR_Gate xnor_1, 2 bits wide
  assign xnor_2_out = ~(in_2 ^ in_3);  // XNOR_Gate xnor_2, 2 bits wide
  or or_1 (or_1_out, in_1[0], in_1[1]);
  assign and_1_out = xnor_1_out & xnor_2_out;  // AND_Gate and_1, 2 bits wide
  and and_2 (winner, and_1_out[0], and_1_out[1], or_1_out);
  assign Who = {2{winner}} & in_3;  // AND_Gate and_3, 2 bits wide
endmodule

module main (
  input  SW_3,
  input  SW_2,
  input  SW_1,
  input  SW_0,
  input  PC_3,
  input  PC_2,
  input  PC_1,
  input  PC_0,
  output Winner_is
);

  wire and_2_out, and_3_out, and_4_out, and_7_out, and_8_out, and_9_out, and_10_out, and_11_out, and_12_out,
       and_13_out, and_14_out, and_15_out, and_17_out, and_18_out, and_19_out, and_20_out, and_21_out,
       and_22_out, and_23_out, and_24_out, and_25_out, clock_1_out, clock_2_out, COMPUTER_PLAY, ILLEGAL_MOVE,
       MUX0, MUX1, MUX2, MUX3, NO_SPACE, nor_1_out, not_1_out, not_2_out, not_3_out, not_4_out, not_5_out,
       not_6_out, not_7_out, not_8_out, not_9_out, not_10_out, or_1_out, or_2_out, or_6_out, or_7_out,
       or_8_out, or_9_out, or_10_out, or_11_out, or_12_out, or_13_out, or_14_out, PC, PC_1_t, PC_2_t, PC_3_t,
       PC_4, PC_5, PC_6, PC_7, PC_8, PC_9, PL_1, PL_2, PL_3, PL_4, PL_5, PL_6, PL_7, PL_8, PL_9, PLAY,
       PLAYER_PLAY, RESET;
  wire [1:0] CURRENT_STATE, multiplexer_1_out, multiplexer_2_out, multiplexer_3_out, multiplexer_4_out,
       multiplexer_5_out, multiplexer_6_out, multiplexer_7_out, multiplexer_8_out, multiplexer_9_out,
       multiplexer_10_out, multiplexer_11_out, multiplexer_12_out, multiplexer_13_out, multiplexer_14_out,
       multiplexer_15_out, multiplexer_16_out, multiplexer_17_out, multiplexer_18_out, multiplexer_19_out,
       multiplexer_20_out, multiplexer_21_out, multiplexer_22_out, Position_1_q, Position_2_q, Position_3_q,
       Position_4_q, Position_5_q, Position_6_q, Position_7_q, Position_8_q, Position_9_q,
       Winner_Detector_who;

  Button u_PC (.out(PC));
  Button u_Play (.out(PLAY));
  not not_1 (not_1_out, PLAY);
  Decoder #(.select(4), .disabled(0)) decoder_1 (
    .out0(PL_1), .out1(PL_2), .out2(PL_3), .out3(PL_4), .out4(PL_5), .out5(PL_6), .out6(PL_7), .out7(PL_8),
    .out8(PL_9), .sel({SW_3, SW_2, SW_1, SW_0}), .en(PLAYER_PLAY));  // open: out9, out10, out11, out12, out13, out14, out15
  Button u_RESET (.out(RESET));
  Decoder #(.select(4), .disabled(0)) decoder_2 (
    .out0(PC_1_t), .out1(PC_2_t), .out2(PC_3_t), .out3(PC_4), .out4(PC_5), .out5(PC_6), .out6(PC_7),
    .out7(PC_8), .out8(PC_9), .sel({PC_3, PC_2, PC_1, PC_0}), .en(COMPUTER_PLAY));  // open: out9, out10, out11, out12, out13, out14, out15
  not not_2 (not_2_out, RESET);
  and and_1 (COMPUTER_PLAY, and_3_out, PC);
  and and_2 (and_2_out, PLAY, not_2_out);
  not not_3 (not_3_out, CURRENT_STATE[0]);
  not not_4 (not_4_out, CURRENT_STATE[1]);
  and and_3 (and_3_out, not_3_out, CURRENT_STATE[1]);
  and and_4 (and_4_out, CURRENT_STATE[0], CURRENT_STATE[1]);
  nor nor_1 (nor_1_out, CURRENT_STATE[0], CURRENT_STATE[1]);
  or or_1 (or_1_out, RESET, not_1_out);
  and and_5 (PLAYER_PLAY, CURRENT_STATE[0], not_4_out);
  Multiplexer #(.width(2), .disabled(0), .enable("false")) multiplexer_1 (
    .in0(Position_1_q), .in1(2'b01), .out(multiplexer_1_out), .sel(PL_1));
  Multiplexer #(.width(2), .disabled(0), .enable("false")) multiplexer_2 (
    .in0(Position_2_q), .in1(2'b01), .out(multiplexer_2_out), .sel(PL_2));
  Multiplexer #(.width(2), .disabled(0), .enable("false")) multiplexer_3 (
    .in0(Position_3_q), .in1(2'b01), .out(multiplexer_3_out), .sel(PL_3));
  Multiplexer #(.width(2), .disabled(0), .enable("false")) multiplexer_4 (
    .in0(Position_4_q), .in1(2'b01), .out(multiplexer_4_out), .sel(PL_4));
  Multiplexer #(.width(2), .disabled(0), .enable("false")) multiplexer_5 (
    .in0(Position_5_q), .in1(2'b01), .out(multiplexer_5_out), .sel(PL_5));
  Multiplexer #(.width(2), .disabled(0), .enable("false")) multiplexer_6 (
    .in0(Position_6_q), .in1(2'b01), .out(multiplexer_6_out), .sel(PL_6));
  Multiplexer #(.width(2), .disabled(0), .enable("false")) multiplexer_7 (
    .in0(Position_7_q), .in1(2'b01), .out(multiplexer_7_out), .sel(PL_7));
  Multiplexer #(.width(2), .disabled(0), .enable("false")) multiplexer_8 (
    .in0(Position_8_q), .in1(2'b01), .out(multiplexer_8_out), .sel(PL_8));
  Multiplexer #(.width(2), .disabled(0), .enable("false")) multiplexer_9 (
    .in0(Position_9_q), .in1(2'b01), .out(multiplexer_9_out), .sel(PL_9));
  and and_6 (MUX1, and_2_out, nor_1_out);
  not not_5 (not_5_out, ILLEGAL_MOVE);
  not not_6 (not_6_out, NO_SPACE);
  not not_7 (not_7_out, Winner_is);
  or or_2 (or_2_out, NO_SPACE, Winner_is);
  not not_8 (not_8_out, RESET);
  Multiplexer #(.width(2), .disabled(0), .enable("false")) multiplexer_10 (
    .in0(multiplexer_1_out), .in1(2'b10), .out(multiplexer_10_out), .sel(PC_1_t));
  Multiplexer #(.width(2), .disabled(0), .enable("false")) multiplexer_11 (
    .in0(multiplexer_3_out), .in1(2'b10), .out(multiplexer_11_out), .sel(PC_3_t));
  Multiplexer #(.width(2), .disabled(0), .enable("false")) multiplexer_12 (
    .in0(multiplexer_4_out), .in1(2'b10), .out(multiplexer_12_out), .sel(PC_4));
  Multiplexer #(.width(2), .disabled(0), .enable("false")) multiplexer_13 (
    .in0(multiplexer_5_out), .in1(2'b10), .out(multiplexer_13_out), .sel(PC_5));
  Multiplexer #(.width(2), .disabled(0), .enable("false")) multiplexer_14 (
    .in0(multiplexer_6_out), .in1(2'b10), .out(multiplexer_14_out), .sel(PC_6));
  Multiplexer #(.width(2), .disabled(0), .enable("false")) multiplexer_15 (
    .in0(multiplexer_7_out), .in1(2'b10), .out(multiplexer_15_out), .sel(PC_7));
  Multiplexer #(.width(2), .disabled(0), .enable("false")) multiplexer_16 (
    .in0(multiplexer_8_out), .in1(2'b10), .out(multiplexer_16_out), .sel(PC_8));
  Multiplexer #(.width(2), .disabled(0), .enable("false")) multiplexer_17 (
    .in0(multiplexer_9_out), .in1(2'b10), .out(multiplexer_17_out), .sel(PC_9));
  and and_7 (and_7_out, nor_1_out, or_1_out);
  and and_8 (and_8_out, PLAYER_PLAY, ILLEGAL_MOVE);
  and and_9 (and_9_out, PLAYER_PLAY, not_5_out);
  not not_9 (not_9_out, PC);
  and and_10 (and_10_out, not_6_out, PC, not_7_out);
  and and_11 (and_11_out, and_4_out, not_8_out);
  and and_12 (and_12_out, and_4_out, RESET);
  Multiplexer #(.width(2), .disabled(0), .enable("false")) multiplexer_18 (
    .in0(multiplexer_2_out), .in1(2'b10), .out(multiplexer_18_out), .sel(PC_2_t));
  Clock clock_1 (.out(clock_1_out));
  or or_3 (MUX2, and_9_out, and_13_out);
  and and_13 (and_13_out, not_9_out, and_3_out);
  and and_14 (and_14_out, and_3_out, and_10_out);
  Register #(.width(2)) Position_1 (
    .D(multiplexer_10_out), .en(not_10_out), .Q(Position_1_q), .clk(clock_1_out), .clr(RESET));
  Register #(.width(2)) Position_2 (
    .D(multiplexer_18_out), .en(not_10_out), .Q(Position_2_q), .clk(clock_1_out), .clr(RESET));
  Register #(.width(2)) Position_3 (
    .D(multiplexer_11_out), .en(not_10_out), .Q(Position_3_q), .clk(clock_1_out), .clr(RESET));
  Register #(.width(2)) Position_4 (
    .D(multiplexer_12_out), .en(not_10_out), .Q(Position_4_q), .clk(clock_1_out), .clr(RESET));
  Register #(.width(2)) Position_5 (
    .D(multiplexer_13_out), .en(not_10_out), .Q(Position_5_q), .clk(clock_1_out), .clr(RESET));
  Register #(.width(2)) Position_6 (
    .D(multiplexer_14_out), .en(not_10_out), .Q(Position_6_q), .clk(clock_1_out), .clr(RESET));
  Register #(.width(2)) Position_7 (
    .D(multiplexer_15_out), .en(not_10_out), .Q(Position_7_q), .clk(clock_1_out), .clr(RESET));
  Register #(.width(2)) Position_8 (
    .D(multiplexer_16_out), .en(not_10_out), .Q(Position_8_q), .clk(clock_1_out), .clr(RESET));
  Register #(.width(2)) Position_9 (
    .D(multiplexer_17_out), .en(not_10_out), .Q(Position_9_q), .clk(clock_1_out), .clr(RESET));
  not not_10 (not_10_out, ILLEGAL_MOVE);
  and and_15 (and_15_out, and_3_out, PC, or_2_out);
  or or_4 (MUX0, and_7_out, and_8_out, and_14_out, and_12_out);
  or or_5 (MUX3, and_15_out, and_11_out);
  Multiplexer #(.width(2), .disabled(0), .enable("false")) multiplexer_19 (
    .in0(CURRENT_STATE), .in1(2'b11), .out(multiplexer_19_out), .sel(MUX3));
  Multiplexer #(.width(2), .disabled(0), .enable("false")) multiplexer_20 (
    .in0(multiplexer_19_out), .in1(2'b10), .out(multiplexer_20_out), .sel(MUX2));
  Multiplexer #(.width(2), .disabled(0), .enable("false")) multiplexer_21 (
    .in0(multiplexer_20_out), .in1(2'b00), .out(multiplexer_21_out), .sel(MUX0));
  Winner_Detector Winner_Detector (
    .in_1(Position_1_q), .in_2(Position_2_q), .in_3(Position_3_q), .in_4(Position_4_q), .in_5(Position_5_q),
    .in_6(Position_6_q), .in_7(Position_7_q), .in_8(Position_8_q), .in_9(Position_9_q), .wi(Winner_is),
    .who(Winner_Detector_who));
  Multiplexer #(.width(2), .disabled(0), .enable("false")) multiplexer_22 (
    .in0(multiplexer_21_out), .in1(2'b01), .out(multiplexer_22_out), .sel(MUX1));
  or or_6 (or_6_out, Position_1_q[0], Position_1_q[1]);
  or or_7 (or_7_out, Position_2_q[0], Position_2_q[1]);
  or or_8 (or_8_out, Position_3_q[0], Position_3_q[1]);
  or or_9 (or_9_out, Position_4_q[0], Position_4_q[1]);
  or or_10 (or_10_out, Position_5_q[0], Position_5_q[1]);
  or or_11 (or_11_out, Position_6_q[0], Position_6_q[1]);
  or or_12 (or_12_out, Position_7_q[0], Position_7_q[1]);
  or or_13 (or_13_out, Position_8_q[0], Position_8_q[1]);
  or or_14 (or_14_out, Position_9_q[0], Position_9_q[1]);
  Register #(.width(2)) FSM_STATES (
    .D(multiplexer_22_out), .Q(CURRENT_STATE), .clk(clock_2_out), .clr(RESET));  // open: en
  Clock clock_2 (.out(clock_2_out));
  LED led_1 (.in(Position_1_q[0]));
  LED led_2 (.in(Position_1_q[1]));
  LED led_3 (.in(Position_4_q[0]));
  LED led_4 (.in(Position_4_q[1]));
  LED led_5 (.in(Position_7_q[0]));
  LED led_6 (.in(Position_7_q[1]));
  LED led_7 (.in(Winner_Detector_who[0]));
  LED led_8 (.in(Winner_Detector_who[1]));
  Hex_Digit_Display hex_digit_display_1 (.value({2'b00, CURRENT_STATE}));  // open: dp
  LED led_9 (.in(Position_2_q[0]));
  LED led_10 (.in(Position_2_q[1]));
  LED led_11 (.in(Position_5_q[0]));
  LED led_12 (.in(Position_5_q[1]));
  LED led_13 (.in(Position_8_q[0]));
  LED led_14 (.in(Position_8_q[1]));
  LED led_15 (.in(Position_3_q[0]));
  LED led_16 (.in(Position_3_q[1]));
  LED led_17 (.in(Position_6_q[0]));
  LED led_18 (.in(Position_6_q[1]));
  LED led_19 (.in(Position_9_q[0]));
  LED led_20 (.in(Position_9_q[1]));
  and and_16 (NO_SPACE, or_6_out, or_7_out, or_8_out, or_9_out, or_10_out, or_11_out, or_12_out, or_13_out, or_14_out);
  and and_17 (and_17_out, PL_1, or_6_out);
  and and_18 (and_18_out, or_7_out, PL_2);
  and and_19 (and_19_out, or_8_out, PL_3);
  and and_20 (and_20_out, or_9_out, PL_4);
  and and_21 (and_21_out, or_10_out, PL_5);
  and and_22 (and_22_out, or_11_out, PL_6);
  and and_23 (and_23_out, or_12_out, PL_7);
  and and_24 (and_24_out, or_13_out, PL_8);
  and and_25 (and_25_out, or_14_out, PL_9);
  or or_15 (ILLEGAL_MOVE, and_17_out, and_18_out, and_19_out, and_20_out, and_21_out, and_22_out, and_23_out, and_24_out, and_25_out);

  // Other names for the same wires on the sheet: WIN = Winner_is
endmodule

module Winner_Detector (
  input  [1:0] in_1,
  input  [1:0] in_2,
  input  [1:0] in_3,
  input  [1:0] in_4,
  input  [1:0] in_5,
  input  [1:0] in_6,
  input  [1:0] in_7,
  input  [1:0] in_8,
  input  [1:0] in_9,
  output wi,
  output [1:0] who
);

  wire n1_case_winner_detect_1_winner, n1_case_winner_detect_2_winner, n1_case_winner_detect_3_winner,
       n1_case_winner_detect_4_winner, n1_case_winner_detect_5_winner, n1_case_winner_detect_6_winner,
       n1_case_winner_detect_7_winner, n1_case_winner_detect_8_winner;
  wire [1:0] n1_case_winner_detect_1_who, n1_case_winner_detect_2_who, n1_case_winner_detect_3_who,
       n1_case_winner_detect_4_who, n1_case_winner_detect_5_who, n1_case_winner_detect_6_who,
       n1_case_winner_detect_7_who, n1_case_winner_detect_8_who;

  _1_case_winner_detect u_1_case_winner_detect_1 (
    .in_1(in_1), .in_2(in_2), .in_3(in_3), .winner(n1_case_winner_detect_1_winner),
    .Who(n1_case_winner_detect_1_who));
  _1_case_winner_detect u_1_case_winner_detect_2 (
    .in_1(in_4), .in_2(in_5), .in_3(in_6), .winner(n1_case_winner_detect_2_winner),
    .Who(n1_case_winner_detect_2_who));
  _1_case_winner_detect u_1_case_winner_detect_3 (
    .in_1(in_7), .in_2(in_8), .in_3(in_9), .winner(n1_case_winner_detect_3_winner),
    .Who(n1_case_winner_detect_3_who));
  _1_case_winner_detect u_1_case_winner_detect_4 (
    .in_1(in_1), .in_2(in_4), .in_3(in_7), .winner(n1_case_winner_detect_4_winner),
    .Who(n1_case_winner_detect_4_who));
  _1_case_winner_detect u_1_case_winner_detect_5 (
    .in_1(in_2), .in_2(in_5), .in_3(in_8), .winner(n1_case_winner_detect_5_winner),
    .Who(n1_case_winner_detect_5_who));
  _1_case_winner_detect u_1_case_winner_detect_6 (
    .in_1(in_3), .in_2(in_6), .in_3(in_9), .winner(n1_case_winner_detect_6_winner),
    .Who(n1_case_winner_detect_6_who));
  _1_case_winner_detect u_1_case_winner_detect_7 (
    .in_1(in_1), .in_2(in_5), .in_3(in_9), .winner(n1_case_winner_detect_7_winner),
    .Who(n1_case_winner_detect_7_who));
  _1_case_winner_detect u_1_case_winner_detect_8 (
    .in_1(in_3), .in_2(in_5), .in_3(in_7), .winner(n1_case_winner_detect_8_winner),
    .Who(n1_case_winner_detect_8_who));
  or or_1 (wi, n1_case_winner_detect_1_winner, n1_case_winner_detect_2_winner, n1_case_winner_detect_3_winner, n1_case_winner_detect_4_winner, n1_case_winner_detect_5_winner, n1_case_winner_detect_6_winner, n1_case_winner_detect_7_winner, n1_case_winner_detect_8_winner);
  assign who = n1_case_winner_detect_1_who | n1_case_winner_detect_2_who | n1_case_winner_detect_3_who | n1_case_winner_detect_4_who | n1_case_winner_detect_5_who | n1_case_winner_detect_6_who | n1_case_winner_detect_7_who | n1_case_winner_detect_8_who;  // OR_Gate or_2, 2 bits wide
endmodule
